# Fritzing sketch raspi door lock (saved by Fritzing 0.9.3b)

parts:
  Raspberry_Pi_1 = Raspberry Pi 3 [part_number=RPI-3-V1.2]
  SW-1 = Vibration sensor module
  J1 = Piezo Speaker
  KY-1 = Keyes Relay [package=THT]
  L1 = Solenoid
  J2 = Power Jack [package=power_jack_smd]
  Q1 = NPN-Transistor [part_number=2n2222 package="TO92 [THT]"]
  R1 = Resistor [tolerance=±5% resistance=1k package="1206 [SMD]"]

nets:
  N1: Raspberry_Pi_1.GIPO26, KY-1.signal
  N2: Raspberry_Pi_1.GND, SW-1.Ground, KY-1.ground, Q1.C
  N3: Raspberry_Pi_1.GIPO24, SW-1.Digital_output
  N4: Raspberry_Pi_1.GIPO23, R1.Pin_1
  5V: Raspberry_Pi_1.5V, SW-1.vcc
  N5: J1.pin2, KY-1.power
  N6: KY-1.C, L1.pin1
  N7: KY-1.NO, L1.pin2, J2.GND, J2.GNDBREAK

notes:
  12 VDC

custom parts:
  Vibration sensor module: Single-roller type full induction trigger switch. When no vibration or tilt, the product is ON conduction state, and in the steady state, when a vibration or tilt, the switch will be rendered instantly disconnect the conductive resistance increases, generating a current pulse signal, thereby triggering circuit. The default state of the swith is close Digital output Supply voltage:3.3V-5V On-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
  Keyes Relay: The Keyes 5V relay module is suitable for SCM development, home appliance control. It uses a 5V~12V TIL control signal which can control DC / AC signal.
